# Fritzing sketch joystick-breadboard (saved by Fritzing 0.9.6b)
breadboards: 1

parts:
  J1 = T Cobbler Plus
  Part1 = Adafruit ADS1115 16Bit I2C ADC [part_number="Adafruit #1085"]
  Mod1 = KY-023 Dual Axis Joystick Module [package="Breakout board"]

nets:
  VDD: J1.5.0V#1, Part1.VDD, Mod1.+5V
  N1: J1.SDA, Part1.SDA
  N2: J1.SCL, Part1.SCL
  GND: J1.GND#5, Part1.GND, Mod1.GND
  N3: Part1.AIN0, Mod1.VRy

notes:
  GND
  +5V
  VRy

custom parts:
  T Cobbler Plus: The T-Cobbler Plus is an add on prototyping board from Adafruit specifically designed for the Raspberry Pi B+ that can break out all those tasty power, GPIO, I2C and SPI pins from the 40-pin header onto a solderless breadboard. This set will make "cobbling together" prototypes with the Pi super easy. The T-Cobbler Plus can plug into any solderless breadboard.
  Adafruit ADS1115 16Bit I2C ADC: For microcontrollers without an analog-to-digital converter or when you want a higher-precision ADC, the ADS1115 provides 16-bit precision at 860 samples/second over I2C. The chip can be configured as 4 single-ended input channels, or two differential channels. As a nice bonus, it even includes a programmable gain amplifier, up to x16, to help boost up smaller single/differential signals to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
  KY-023 Dual Axis Joystick Module: KY-023 Dual-Axis Joystick Module.
