# Fritzing sketch einparkhilfe (saved by Fritzing 0.9.6b)
breadboards: 1

parts:
  J1 = T Cobbler Plus
  Part1 = SRF05 Ultrasonic Rangefinder
  Mod1 = KY-012 Active Buzzer Module [package="Breakout board"]
  Mod2 = KY-004 Key Switch Module [package="Breakout board"]
  Mod3 = KY-029 Dual Color LED Module [package="Breakout board"]
  IC1 = IC, DIP package, 12 pins [chip_label="KY-051 LS"]

nets:
  N1: J1.3V3, Mod2.-, IC1.pin12
  N2: J1.5.0V#1, Part1.VCC, IC1.pin1
  N3: J1.GND#5, Part1.GND, Mod3.G
  N4: J1.GND#8, Mod1.-, IC1.pin7
  N5: J1.#23, Mod2.S
  N6: J1.MOSI, IC1.pin8
  N7: J1.MISO, IC1.pin9
  N8: J1.CE0, Mod3.-
  N9: J1.CE1, Mod3.R
  N10: J1.#13, Mod1.S
  N11: Part1.Trig, IC1.pin5
  N12: Part1.Echo, IC1.pin4

notes:
  KY-012 Buzzer
  KY-051 Level Shifter
  VCCa, A1, A2, A3, A4, GND
  VCCb, B1, B2, B3, B4, OE
  KY-004
  KY-029 LED

custom parts:
  T Cobbler Plus: The T-Cobbler Plus is an add on prototyping board from Adafruit specifically designed for the Raspberry Pi B+ that can break out all those tasty power, GPIO, I2C and SPI pins from the 40-pin header onto a solderless breadboard. This set will make "cobbling together" prototypes with the Pi super easy. The T-Cobbler Plus can plug into any solderless breadboard.
  KY-012 Active Buzzer Module: Active Piezoelectric Buzzer Module KY-012, it produces single-tone sound when signal is high. (Special thanks to vanepp for fixing the PCB holes and other errors)
  KY-004 Key Switch Module: Arduino Key Switch Module Keyes KY-004 is a push button that will output a high signal when pressed.
  KY-029 Dual Color LED Module: KY-029 Dual Color LED Module consist of a common cathode 5mm red/green LED.
