# Fritzing sketch hindernisdetektor (saved by Fritzing 0.9.2b)
breadboards: 1

parts:
  Part1 = Adafruit T-Cobbler Plus [part_number="Adafruit #1989 and #2028"]
  KY-011 = Header 3 [part_number="2-Farb LED" package=screwterminal-3.5mm-3_lock.007s]
  KY-032 = Header 4 [part_number=Hindernisdetektor package=screwterminal-3.5mm-4_lock]
  R1 = Resistor [tolerance=±5% resistance=330 package="1206 [SMD]"]
  R2 = Resistor [tolerance=±5% resistance=330 package="1206 [SMD]"]

nets:
  N1: Part1.+3.3V, KY-032.2
  N2: Part1.GND, KY-011.1, KY-032.1
  N3: Part1.SCLK, KY-032.3
  N4: Part1.GPIO23, R2.Pin_1
  N5: Part1.GPIO24, R1.Pin_1
  N6: KY-011.2, R2.Pin_0
  N7: KY-011.3, R1.Pin_0

notes:
  GND, VCC, Digital, Analog
  GND, Rot, Grün

custom parts:
  Adafruit T-Cobbler Plus: The Raspberry Pi has landed on the Maker World like a 40-GPIO pinned, quad-USB ported, credit card sized bomb of DIY joy. And while you can use most of our great Model B accessories by hooking up our downgrade cable, its probably a good time to upgrade your set up and accessorize using all of the 40 pins. That's why we now carry the Assembled Adafruit Pi T-Cobbler Plus - Breakout + Cable for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
